// Logisim project hw4.circ as structural Verilog: 5 circuits, main circuit main
module main (
  input  reset
);

  wire alu_1_bigor, alu_1_lastbit, ALUin2, and_1_out, and_2_out, BAD, BLT, BNE, clk, decoder_1_out0,
       decoder_1_out1, decoder_1_out2, decoder_1_out3, decoder_1_out4, decoder_1_out5, decoder_1_out6,
       decoder_1_out9, DMwe, In, JAL, JP, JR, not_2_out, not_3_out, or_1_out, Out, Rdst, Rwd, Rwe;
  wire [2:0] multiplexer_1_out, multiplexer_2_out, shift;
  wire [6:0] keyboard_1_data;
  wire [15:0] adder_1_out, alu_1_result, bit_extender_1_out, bit_extender_2_out, bit_extender_3_out,
       bit_extender_4_out, multiplexer_3_out, multiplexer_4_out, multiplexer_5_out, multiplexer_6_out,
       multiplexer_7_out, multiplexer_8_out, multiplexer_9_out, multiplexer_10_out, multiplexer_11_out,
       n1_1_new_address, pc_1_output, ram_1_data, registerfile_1_readdata1, registerfile_1_readdata2;
  wire [15:3] rom_1_data;

  pc pc_1 (.\input (multiplexer_7_out), .clk(clk), .reset(reset), .\output (pc_1_output));
  Clock clock_1 (.out(clk));
  Keyboard keyboard_1 (.clk(clk), .re(In), .clr(reset), .data(keyboard_1_data));  // open: avail
  _1 u_1_1 (.Address(pc_1_output), .new_address(n1_1_new_address));
  assign {bit_extender_1_out[15:8], BAD, bit_extender_1_out[6:0]} = {{9{1'b0}}, keyboard_1_data};  // Bit_Extender bit_extender_1
  or or_1 (or_1_out, decoder_1_out0, decoder_1_out1, decoder_1_out3, decoder_1_out4, decoder_1_out5, decoder_1_out6);
  not not_1 (Rdst, or_1_out);
  or or_2 (Rwe, decoder_1_out0, decoder_1_out1, decoder_1_out2, decoder_1_out3, decoder_1_out4, decoder_1_out6, decoder_1_out5, Rwd, JAL, JR, In);
  assign bit_extender_2_out = {{4{1'b0}}, {rom_1_data[11:3], shift}};  // Bit_Extender bit_extender_2
  ROM #(.addrWidth(16), .dataWidth(16)) rom_1 (.addr(pc_1_output), .data({rom_1_data, shift}));  // open: sel
  Multiplexer #(.width(3), .enable("false")) multiplexer_1 (
    .in0(rom_1_data[5:3]), .in1(rom_1_data[8:6]), .out(multiplexer_1_out), .sel(Rdst));
  assign bit_extender_3_out = {{10{rom_1_data[5]}}, {rom_1_data[5:3], shift}};  // Bit_Extender bit_extender_3
  Decoder #(.select(4), .enable("false")) decoder_1 (
    .out0(decoder_1_out0), .out1(decoder_1_out1), .out2(decoder_1_out2), .out3(decoder_1_out3),
    .out4(decoder_1_out4), .out5(decoder_1_out5), .out6(decoder_1_out6), .out7(Rwd), .out8(DMwe),
    .out9(decoder_1_out9), .out10(JAL), .out11(JR), .out12(BNE), .out13(BLT), .out14(In), .out15(Out),
    .sel(rom_1_data[15:12]));
  Multiplexer #(.width(3), .enable("false")) multiplexer_2 (
    .in0(multiplexer_1_out), .in1(3'b111), .out(multiplexer_2_out), .sel(JAL));
  not not_2 (not_2_out, clk);
  assign bit_extender_4_out = {{9{1'b0}}, bit_extender_1_out[6:0]};  // Bit_Extender bit_extender_4
  Adder #(.width(16)) adder_1 (.a(n1_1_new_address), .b(bit_extender_3_out), .out(adder_1_out));  // open: cin, cout
  and and_1 (and_1_out, BNE, alu_1_bigor);
  Multiplexer #(.width(16), .enable("false")) multiplexer_3 (
    .in0(multiplexer_11_out), .in1(n1_1_new_address), .out(multiplexer_3_out), .sel(JAL));
  or or_3 (JP, JAL, decoder_1_out9);
  or or_4 (ALUin2, Out, In, DMwe, Rwd, decoder_1_out2);
  Multiplexer #(.width(16), .enable("false")) multiplexer_4 (
    .in0(n1_1_new_address), .in1(adder_1_out), .out(multiplexer_4_out), .sel(and_1_out));
  Multiplexer #(.width(16), .enable("false")) multiplexer_5 (
    .in0(multiplexer_4_out), .in1(bit_extender_2_out), .out(multiplexer_5_out), .sel(JP));
  Multiplexer #(.width(16), .enable("false")) multiplexer_6 (
    .in0(multiplexer_5_out), .in1(adder_1_out), .out(multiplexer_6_out), .sel(and_2_out));
  Multiplexer #(.width(16), .enable("false")) multiplexer_7 (
    .in0(multiplexer_6_out), .in1(registerfile_1_readdata1), .out(multiplexer_7_out), .sel(JR));
  and and_2 (and_2_out, BLT, alu_1_lastbit);
  RegisterFile registerfile_1 (
    .ReadReg1(rom_1_data[11:9]), .ReadReg2(rom_1_data[8:6]), .WriteReg(multiplexer_2_out),
    .ReadData1(registerfile_1_readdata1), .ReadData2(registerfile_1_readdata2),
    .WriteData(multiplexer_3_out), .RegWriteEnable(Rwe), .reset(reset), .clk(not_2_out));
  Multiplexer #(.width(16), .enable("false")) multiplexer_8 (
    .in0(registerfile_1_readdata2), .in1(bit_extender_3_out), .out(multiplexer_8_out), .sel(ALUin2));
  Multiplexer #(.width(16), .enable("false")) multiplexer_9 (
    .in0(multiplexer_8_out), .in1(bit_extender_4_out), .out(multiplexer_9_out), .sel(In));
  TTY #(.rows(13), .cols(80), .trigger("falling")) tty_1 (
    .data(registerfile_1_readdata1[6:0]), .clk(clk), .we(Out), .clr(reset));
  Multiplexer #(.width(16), .enable("false")) multiplexer_10 (
    .in0(multiplexer_9_out), .in1(16'h80), .out(multiplexer_10_out), .sel(BAD));
  ALU alu_1 (
    .a(registerfile_1_readdata1), .b(multiplexer_10_out), .shift(shift), .Result(alu_1_result),
    .bigOR(alu_1_bigor), .lastbit(alu_1_lastbit), .ALUop(rom_1_data[15:12]));
  not not_3 (not_3_out, clk);
  RAM #(.addrWidth(16), .dataWidth(16), .bus("separate")) ram_1 (
    .addr(alu_1_result), .din(registerfile_1_readdata2), .data(ram_1_data), .str(DMwe), .clk(not_3_out));  // open: sel, ld, clr
  Multiplexer #(.width(16), .enable("false")) multiplexer_11 (
    .in0(alu_1_result), .in1(ram_1_data), .out(multiplexer_11_out), .sel(Rwd));

  // Notes on the sheet:
  //   contents of rom_1 (hex, n*v repeats v):
  //   2190 6c34 6c37 a007 c1ff 2fc1 c1ff 2042 a01d 2043 2141 2083 5219 d4c1 9015 a03e c802 2140 9015 2482
  //   900c ca01 9018 a01d 2242 900a c1ff 2fc1 c1ff 2dba 8c40 8c81 8cc2 8d03 8d44 8dc5 2140 6a2d 2b40 6a2d
  //   2b40 6a29 2b40 2b47 208a a03e 291e 2912 2b7f 8b00 2640 c238 2a40 a046 7c40 7c81 7cc2 7d03 7d44 7dc5
  //   2d86 be00 20ff 2300 d803 48a0 26c1 9040 38a0 be00 2dbe 8c40 8c81 7280 c401 904f f400 2241 9049 208a
  //   f400 7c40 7c81 2d82 be00
endmodule

module ALU (
  input  [15:0] a,
  input  [15:0] b,
  input  [2:0] shift,
  input  [3:0] ALUop,
  output [15:0] Result,
  output bigOR,
  output lastbit
);

  wire [3:0] bit_extender_1_out;
  wire [14:0] subtractor_1_out;
  wire [15:0] adder_1_out, not_1_out, or_1_out, shifter_1_out, shifter_2_out, xor_1_out;

  assign bit_extender_1_out = {{1{1'b0}}, shift};  // Bit_Extender bit_extender_1
  assign not_1_out = ~a;  // NOT_Gate not_1, 16 bits wide
  assign xor_1_out = a ^ b;  // XOR_Gate xor_1, 16 bits wide
  Adder #(.width(16)) adder_1 (.a(a), .b(b), .out(adder_1_out));  // open: cin, cout
  Subtractor #(.width(16)) subtractor_1 (.a(a), .b(b), .out({lastbit, subtractor_1_out}));  // open: bin, bout
  Shifter #(.width(16), .shift("ar")) shifter_1 (.in(a), .\dist (bit_extender_1_out), .out(shifter_1_out));
  Shifter #(.width(16)) shifter_2 (.in(a), .\dist (bit_extender_1_out), .out(shifter_2_out));
  Multiplexer #(.select(4), .width(16)) multiplexer_1 (
    .in0(not_1_out), .in1(xor_1_out), .in2(adder_1_out), .in3(adder_1_out),
    .in4({lastbit, subtractor_1_out}), .in5(shifter_1_out), .in6(shifter_2_out), .in7(adder_1_out),
    .in8(adder_1_out), .out(Result), .sel(ALUop));  // open: in9, in10, in11, in12, in13, in14, in15, en
  assign or_1_out = {lastbit, subtractor_1_out} | {16{1'b0}};  // OR_Gate or_1, 16 bits wide
  or or_2 (bigOR, or_1_out[0], or_1_out[1], or_1_out[2], or_1_out[3], or_1_out[4], or_1_out[5], or_1_out[6], or_1_out[7], or_1_out[8], or_1_out[9], or_1_out[10], or_1_out[11], or_1_out[12], or_1_out[13], or_1_out[14], or_1_out[15]);
endmodule

module RegisterFile (
  input  [2:0] ReadReg1,
  input  [2:0] ReadReg2,
  input  [15:0] WriteData,
  input  [2:0] WriteReg,
  input  clk,
  input  RegWriteEnable,
  input  reset,
  output [15:0] ReadData1,
  output [15:0] ReadData2
);

  wire and_1_out, and_2_out, and_3_out, and_4_out, and_5_out, and_6_out, and_7_out, read1_0, read1_1,
       read1_2, read1_3, read1_4, read1_5, read1_6, read1_7, read2_0, read2_1, read2_2, read2_3, read2_4,
       read2_5, read2_6, read2_7, write1, write2, write3, write4, write5, write6, write7;
  wire [15:0] register_1_q, register_2_q, register_3_q, register_4_q, register_5_q, register_6_q,
       register_7_q, register_8_q;

  Decoder #(.select(3), .enable("false")) decoder_1 (
    .out0(read1_0), .out1(read1_1), .out2(read1_2), .out3(read1_3), .out4(read1_4), .out5(read1_5),
    .out6(read1_6), .out7(read1_7), .sel(ReadReg1));
  Decoder #(.select(3), .enable("false")) decoder_2 (
    .out0(read2_0), .out1(read2_1), .out2(read2_2), .out3(read2_3), .out4(read2_4), .out5(read2_5),
    .out6(read2_6), .out7(read2_7), .sel(ReadReg2));
  Decoder #(.select(3), .enable("false")) decoder_3 (
    .out1(write1), .out2(write2), .out3(write3), .out4(write4), .out5(write5), .out6(write6), .out7(write7),
    .sel(WriteReg));  // open: out0
  and and_1 (and_1_out, write1, RegWriteEnable);
  and and_2 (and_2_out, write2, RegWriteEnable);
  and and_3 (and_3_out, write3, RegWriteEnable);
  and and_4 (and_4_out, write4, RegWriteEnable);
  and and_5 (and_5_out, write5, RegWriteEnable);
  and and_6 (and_6_out, write6, RegWriteEnable);
  and and_7 (and_7_out, write7, RegWriteEnable);
  Register #(.width(16), .trigger("falling")) register_1 (
    .D({16{1'b0}}), .Q(register_1_q), .clk(clk), .clr(reset));  // open: en
  Register #(.width(16), .trigger("falling")) register_2 (
    .D(WriteData), .en(and_1_out), .Q(register_2_q), .clk(clk), .clr(reset));
  Register #(.width(16), .trigger("falling")) register_3 (
    .D(WriteData), .en(and_2_out), .Q(register_3_q), .clk(clk), .clr(reset));
  Register #(.width(16), .trigger("falling")) register_4 (
    .D(WriteData), .en(and_3_out), .Q(register_4_q), .clk(clk), .clr(reset));
  Register #(.width(16), .trigger("falling")) register_5 (
    .D(WriteData), .en(and_4_out), .Q(register_5_q), .clk(clk), .clr(reset));
  Register #(.width(16), .trigger("falling")) register_6 (
    .D(WriteData), .en(and_5_out), .Q(register_6_q), .clk(clk), .clr(reset));
  Register #(.width(16), .trigger("falling")) register_7 (
    .D(WriteData), .en(and_6_out), .Q(register_7_q), .clk(clk), .clr(reset));
  Register #(.width(16), .trigger("falling")) register_8 (
    .D(WriteData), .en(and_7_out), .Q(register_8_q), .clk(clk), .clr(reset));
  // Probe on register_1_q
  // Probe on register_2_q
  // Probe on register_3_q
  // Probe on register_4_q
  // Probe on register_5_q
  // Probe on register_6_q
  // Probe on register_7_q
  // Probe on register_8_q
  assign ReadData1 = read1_0 ? register_1_q : 16'bz;  // Controlled_Buffer controlled_buffer_1
  assign ReadData2 = read2_0 ? register_1_q : 16'bz;  // Controlled_Buffer controlled_buffer_2
  assign ReadData1 = read1_1 ? register_2_q : 16'bz;  // Controlled_Buffer controlled_buffer_3
  assign ReadData2 = read2_1 ? register_2_q : 16'bz;  // Controlled_Buffer controlled_buffer_4
  assign ReadData1 = read1_2 ? register_3_q : 16'bz;  // Controlled_Buffer controlled_buffer_5
  assign ReadData2 = read2_2 ? register_3_q : 16'bz;  // Controlled_Buffer controlled_buffer_6
  assign ReadData1 = read1_3 ? register_4_q : 16'bz;  // Controlled_Buffer controlled_buffer_7
  assign ReadData2 = read2_3 ? register_4_q : 16'bz;  // Controlled_Buffer controlled_buffer_8
  assign ReadData1 = read1_4 ? register_5_q : 16'bz;  // Controlled_Buffer controlled_buffer_9
  assign ReadData2 = read2_4 ? register_5_q : 16'bz;  // Controlled_Buffer controlled_buffer_10
  assign ReadData1 = read1_5 ? register_6_q : 16'bz;  // Controlled_Buffer controlled_buffer_11
  assign ReadData2 = read2_5 ? register_6_q : 16'bz;  // Controlled_Buffer controlled_buffer_12
  assign ReadData1 = read1_6 ? register_7_q : 16'bz;  // Controlled_Buffer controlled_buffer_13
  assign ReadData2 = read2_6 ? register_7_q : 16'bz;  // Controlled_Buffer controlled_buffer_14
  assign ReadData1 = read1_7 ? register_8_q : 16'bz;  // Controlled_Buffer controlled_buffer_15
  assign ReadData2 = read2_7 ? register_8_q : 16'bz;  // Controlled_Buffer controlled_buffer_16

  // Other names for the same wires on the sheet: E = RegWriteEnable
endmodule

// PC
module pc (
  input  [15:0] \input ,
  input  clk,
  input  reset,
  output [15:0] \output 
);

  D_Flip_Flop d_ff_1 (.clk(clk), .D(\input [0]), .Q(\output [0]), .en(1'b1), .reset(reset));  // open: Qn, preset
  D_Flip_Flop d_ff_2 (.clk(clk), .D(\input [1]), .Q(\output [1]), .en(1'b1), .reset(reset));  // open: Qn, preset
  D_Flip_Flop d_ff_3 (.clk(clk), .D(\input [2]), .Q(\output [2]), .en(1'b1), .reset(reset));  // open: Qn, preset
  D_Flip_Flop d_ff_4 (.clk(clk), .D(\input [3]), .Q(\output [3]), .en(1'b1), .reset(reset));  // open: Qn, preset
  D_Flip_Flop d_ff_5 (.clk(clk), .D(\input [4]), .Q(\output [4]), .en(1'b1), .reset(reset));  // open: Qn, preset
  D_Flip_Flop d_ff_6 (.clk(clk), .D(\input [5]), .Q(\output [5]), .en(1'b1), .reset(reset));  // open: Qn, preset
  D_Flip_Flop d_ff_7 (.clk(clk), .D(\input [6]), .Q(\output [6]), .en(1'b1), .reset(reset));  // open: Qn, preset
  D_Flip_Flop d_ff_8 (.clk(clk), .D(\input [7]), .Q(\output [7]), .en(1'b1));  // open: Qn, preset, reset
  D_Flip_Flop d_ff_9 (.clk(clk), .D(\input [8]), .Q(\output [8]), .en(1'b1), .reset(reset));  // open: Qn, preset
  D_Flip_Flop d_ff_10 (.clk(clk), .D(\input [9]), .Q(\output [9]), .en(1'b1), .reset(reset));  // open: Qn, preset
  D_Flip_Flop d_ff_11 (.clk(clk), .D(\input [10]), .Q(\output [10]), .en(1'b1), .reset(reset));  // open: Qn, preset
  D_Flip_Flop d_ff_12 (.clk(clk), .D(\input [11]), .Q(\output [11]), .en(1'b1), .reset(reset));  // open: Qn, preset
  D_Flip_Flop d_ff_13 (.clk(clk), .D(\input [12]), .Q(\output [12]), .en(1'b1), .reset(reset));  // open: Qn, preset
  D_Flip_Flop d_ff_14 (.clk(clk), .D(\input [13]), .Q(\output [13]), .en(1'b1), .reset(reset));  // open: Qn, preset
  D_Flip_Flop d_ff_15 (.clk(clk), .D(\input [14]), .Q(\output [14]), .en(1'b1), .reset(reset));  // open: Qn, preset
  D_Flip_Flop d_ff_16 (.clk(clk), .D(\input [15]), .Q(\output [15]), .en(1'b1), .reset(reset));  // open: Qn, preset
endmodule

module _1 (
  input  [15:0] Address,
  output [15:0] new_address
);

  Adder #(.width(16)) adder_1 (.a(16'h1), .b(Address), .out(new_address));  // open: cin, cout
endmodule
